# Fritzing sketch Bluetooth (saved by Fritzing 0.9.3b)

parts:
  Componente1 = Arduino Uno (Rev3)
  Componente3 = Bluetooth HC-06

nets:
  N1: Componente1.D0/RX, Componente3.TXD
  N2: Componente1.D1/TX, Componente3.RXD
  5V: Componente1.5V, Componente3.VCC
  GND: Componente1.GND, Componente3.GND
