# Fritzing sketch Sensor (saved by Fritzing 0.9.3b)

parts:
  Componente1 = Arduino Uno (Rev3)
  YF-S201_Flow_Meter1 = YF-S201 Water Flow Meter

nets:
  N1: Componente1.D2, YF-S201_Flow_Meter1.SIG
  5V: Componente1.5V, YF-S201_Flow_Meter1.VCC
  GND: Componente1.GND, YF-S201_Flow_Meter1.GND

custom parts:
  YF-S201 Water Flow Meter: The YF-S201 Flow Meter. The input voltage is 5V to 24V (DC).
