# Fritzing sketch Tudocom nome (saved by Fritzing 0.9.3b)

parts:
  Componente1 = Arduino Uno (Rev3)
  VALVE1 = Plastic Solenoid Valve
  KY-3 = Keyes Relay [package=THT]
  YF-S201_Flow_Meter1 = YF-S201 Water Flow Meter
  Componente2 = Bluetooth HC-06
  S4 = Round Pushbutton
  S5 = Round Pushbutton
  S6 = Round Pushbutton
  J1 = Piezo Speaker

nets:
  GND: Componente1.GND, KY-3.ground, YF-S201_Flow_Meter1.GND, Componente2.GND, J1.pin1
  N1: Componente1.D0/RX, Componente2.TXD
  N2: Componente1.D1/TX, Componente2.RXD
  N3: Componente1.D2, YF-S201_Flow_Meter1.SIG
  N4: Componente1.D3_PWM, S4.leg1
  N5: Componente1.D4, S6.leg1
  N6: Componente1.D5_PWM, S5.leg1
  N7: Componente1.D6_PWM, J1.pin2
  N8: Componente1.D7, KY-3.signal
  VCC: Componente1.5V, KY-3.power, YF-S201_Flow_Meter1.VCC, Componente2.VCC
  N9: VALVE1.no_name_yet#2, KY-3.NO
  N10: S4.leg0, S5.leg0, S6.leg0

notes:
  127 V
  LIGA
  PAUSE
  DESLIGA
  Relé
  Sensor de fluxo
  Valvula Solenoide
  Módulo Bluetooth
  Buzzer Piezo
  ARDUINO UNO

custom parts:
  Keyes Relay: The Keyes 5V relay module is suitable for SCM development, home appliance control. It uses a 5V~12V TIL control signal which can control DC / AC signal.
  YF-S201 Water Flow Meter: The YF-S201 Flow Meter. The input voltage is 5V to 24V (DC).
