# Fritzing sketch Valvula (saved by Fritzing 0.9.3b)

parts:
  Componente1 = Arduino Uno (Rev3)
  VALVE1 = Plastic Solenoid Valve
  KY-3 = Keyes Relay [package=THT]

nets:
  N1: Componente1.D7, KY-3.signal
  N2: Componente1.5V, KY-3.power
  N3: Componente1.GND, KY-3.ground
  N4: VALVE1.no_name_yet#2, KY-3.NO

notes:
  127 V

custom parts:
  Keyes Relay: The Keyes 5V relay module is suitable for SCM development, home appliance control. It uses a 5V~12V TIL control signal which can control DC / AC signal.
