# Fritzing sketch botoes (saved by Fritzing 0.9.3b)

parts:
  Componente1 = Arduino Uno (Rev3)
  S1 = Round Pushbutton
  S2 = Round Pushbutton
  S3 = Round Pushbutton

nets:
  N1: Componente1.GND, S1.leg0, S2.leg0, S3.leg0
  N2: Componente1.D3_PWM, S1.leg1
  N3: Componente1.D4, S2.leg1
  N4: Componente1.D5_PWM, S3.leg1
